# Fritzing sketch p3 (saved by Fritzing 0.9.3b)
breadboards: 1

parts:
  V1 = DC Power [voltage=5]
  R1 = Resistor [tolerance=±5% resistance=220 package=THT]
  R2 = Resistor [tolerance=±5% resistance=220 package=THT]
  V2 = DC Power [voltage=5]
  R3 = Resistor [tolerance=±5% resistance=220 package=THT]
  R4 = Resistor [tolerance=±5% resistance=220 package=THT]

nets:
  N1: V1.V+, R1.Pin_0, R2.Pin_0
  GND: V1.V-, R1.Pin_1, R2.Pin_1
  N2: V2.V+, R3.Pin_0
  N3: V2.V-, R4.Pin_1
  N4: R3.Pin_1, R4.Pin_0

notes:
  Reihenschaltung
  Parallelschaltung
