# Fritzing sketch p4 (saved by Fritzing 0.9.3b)
breadboards: 1

parts:
  D2 = Zener Diode [part_number=1N4732A breakdown_voltage=3.6V package="300 mil [THT]"]
  LED1 = LED - 3mm [color="Red (633nm)" package="3 mm [THT]"]
  U1 = DC Power [voltage=5]
  U1_2 = DC Power [voltage=5]

nets:
  N1: D2.cathode, U1.V-
  N2: D2.anode, U1.V+
  GND: LED1.cathode, U1_2.V-
  N3: LED1.anode, U1_2.V+
