# Fritzing sketch P2 (saved by Fritzing 0.9.3b)
breadboards: 1

parts:
  V1 = DC Power [voltage=5]
  R1 = Resistor [tolerance=±5% resistance=220 package=THT]
  Bauteil1 = Lilypad Power Supply

nets:
  N1: V1.V+, R1.Pin_0, Bauteil1.+
  GND: V1.V-, R1.Pin_1, Bauteil1.GND
